# Fritzing sketch rtc-dht-I2C (saved by Fritzing 0.9.9b)
breadboards: 1

parts:
  DHT1 = Humidity and Temperature Sensor DHT11
  IC1 = ks0172 [chip_label=?]
  ZS-042_RTC1 = ZS-042 RTC Module
  LCD2004-I2C1 = LCD2004-I2C

nets:
  N1: DHT1.Vcc, IC1.5V#60
  N2: DHT1.Data-signal, IC1.9
  N3: DHT1.GND_1, IC1.GND#74
  N4: IC1.SDA, ZS-042_RTC1.SDA, LCD2004-I2C1.SDA
  N5: IC1.SCL, ZS-042_RTC1.SCL, LCD2004-I2C1.SCL
  VCC: IC1.5V#93, ZS-042_RTC1.VCC, LCD2004-I2C1.VCC
  GND: IC1.GND#94, ZS-042_RTC1.GND, LCD2004-I2C1.GND

custom parts:
  Humidity and Temperature Sensor DHT11: Digital relative humidity & temperature sensor DHT11
  ks0172: Arduino UNO R3 extra pins
  LCD2004-I2C: A standard character display with 4x20 characters. Comes in many colors with LCM2004 IIC attached.
